// Logisim project project.circ as structural Verilog: 3 circuits, main circuit main
module main (
);

  MyRAM myram_1 ();  // open: Mode, Address0, Address1, Input0, Input1, Input2, Input3, Output0, Output1, Output2, Output3
  MyALU myalu_1 ();  // open: Operation1, AInvert, BInvert, Operation0, A0, B0, A1, B1, A2, B2, A3, B3, Result0, Result1, Result2, Result3, Status0_Sign, Status1_Zero, Status2_SignOverflow
endmodule

module MyRAM (
  input  Mode,
  input  Address0,
  input  Address1,
  input  Input0,
  input  Input1,
  input  Input2,
  input  Input3,
  output Output0,
  output Output1,
  output Output2,
  output Output3
);

  wire and_1_out, and_2_out, and_3_out, and_4_out, and_5_out, and_6_out, and_7_out, and_8_out, and_9_out,
       and_10_out, and_11_out, and_12_out, and_13_out, and_14_out, and_15_out, and_16_out, and_17_out,
       and_18_out, and_19_out, and_20_out, and_21_out, and_22_out, and_23_out, and_24_out, and_25_out,
       and_26_out, and_27_out, and_28_out, and_29_out, and_30_out, and_31_out, and_32_out, and_33_out,
       and_34_out, and_35_out, and_36_out, and_37_out, and_38_out, and_39_out, and_40_out, and_41_out,
       clock_1_out, d_ff_1_q, d_ff_1_qn, d_ff_2_q, d_ff_3_q, d_ff_4_q, d_ff_5_q, d_ff_6_q, d_ff_7_q,
       d_ff_8_q, d_ff_9_q, d_ff_10_q, d_ff_11_q, d_ff_12_q, d_ff_13_q, d_ff_14_q, d_ff_15_q, d_ff_16_q,
       d_ff_17_q, d_ff_18_q, d_ff_19_q, d_ff_20_q, d_ff_21_q, d_ff_22_q, d_ff_23_q, not_1_out, not_2_out,
       not_3_out, not_4_out, or_1_out, or_2_out, or_3_out, or_4_out;

  Clock clock_1 (.out(clock_1_out));
  D_Flip_Flop d_ff_1 (.D(Mode), .clk(clock_1_out), .Q(d_ff_1_q), .Qn(d_ff_1_qn));  // open: preset, reset
  D_Flip_Flop d_ff_2 (.D(Address0), .clk(clock_1_out), .Q(d_ff_2_q));  // open: Qn, preset, reset
  D_Flip_Flop d_ff_3 (.D(Address1), .clk(clock_1_out), .Q(d_ff_3_q));  // open: Qn, preset, reset
  D_Flip_Flop d_ff_4 (.D(Input0), .clk(clock_1_out), .Q(d_ff_4_q));  // open: Qn, preset, reset
  D_Flip_Flop d_ff_5 (.D(Input1), .clk(clock_1_out), .Q(d_ff_5_q));  // open: Qn, preset, reset
  D_Flip_Flop d_ff_6 (.D(Input2), .clk(clock_1_out), .Q(d_ff_6_q));  // open: Qn, preset, reset
  D_Flip_Flop d_ff_7 (.D(Input3), .clk(clock_1_out), .Q(d_ff_7_q));  // open: Qn, preset, reset
  and and_1 (and_1_out, d_ff_3_q, d_ff_2_q);
  D_Flip_Flop d_ff_8 (.D(d_ff_4_q), .clk(and_2_out), .Q(d_ff_8_q));  // open: Qn, preset, reset
  and and_2 (and_2_out, and_1_out, d_ff_1_qn, clock_1_out);
  D_Flip_Flop d_ff_9 (.D(d_ff_5_q), .clk(and_3_out), .Q(d_ff_9_q));  // open: Qn, preset, reset
  and and_3 (and_3_out, and_1_out, d_ff_1_qn, clock_1_out);
  D_Flip_Flop d_ff_10 (.D(d_ff_6_q), .clk(and_4_out), .Q(d_ff_10_q));  // open: Qn, preset, reset
  and and_4 (and_4_out, and_1_out, d_ff_1_qn, clock_1_out);
  D_Flip_Flop d_ff_11 (.D(d_ff_7_q), .clk(and_5_out), .Q(d_ff_11_q));  // open: Qn, preset, reset
  and and_5 (and_5_out, and_1_out, d_ff_1_qn, clock_1_out);
  and and_6 (and_6_out, and_1_out, d_ff_1_q);
  and and_7 (and_7_out, d_ff_8_q, and_6_out);
  and and_8 (and_8_out, d_ff_9_q, and_6_out);
  and and_9 (and_9_out, d_ff_10_q, and_6_out);
  and and_10 (and_10_out, d_ff_11_q, and_6_out);
  not not_1 (not_1_out, d_ff_2_q);
  and and_11 (and_11_out, d_ff_3_q, not_1_out);
  D_Flip_Flop d_ff_12 (.D(d_ff_4_q), .clk(and_12_out), .Q(d_ff_12_q));  // open: Qn, preset, reset
  and and_12 (and_12_out, and_11_out, d_ff_1_qn, clock_1_out);
  D_Flip_Flop d_ff_13 (.D(d_ff_5_q), .clk(and_13_out), .Q(d_ff_13_q));  // open: Qn, preset, reset
  and and_13 (and_13_out, and_11_out, d_ff_1_qn, clock_1_out);
  D_Flip_Flop d_ff_14 (.D(d_ff_6_q), .clk(and_14_out), .Q(d_ff_14_q));  // open: Qn, preset, reset
  and and_14 (and_14_out, and_11_out, d_ff_1_qn, clock_1_out);
  D_Flip_Flop d_ff_15 (.D(d_ff_7_q), .clk(and_15_out), .Q(d_ff_15_q));  // open: Qn, preset, reset
  and and_15 (and_15_out, and_11_out, d_ff_1_qn, clock_1_out);
  and and_16 (and_16_out, and_11_out, d_ff_1_q);
  and and_17 (and_17_out, d_ff_12_q, and_16_out);
  and and_18 (and_18_out, d_ff_13_q, and_16_out);
  and and_19 (and_19_out, d_ff_14_q, and_16_out);
  and and_20 (and_20_out, d_ff_15_q, and_16_out);
  not not_2 (not_2_out, d_ff_3_q);
  and and_21 (and_21_out, not_2_out, d_ff_2_q);
  D_Flip_Flop d_ff_16 (.D(d_ff_4_q), .clk(and_22_out), .Q(d_ff_16_q));  // open: Qn, preset, reset
  and and_22 (and_22_out, and_21_out, d_ff_1_qn, clock_1_out);
  D_Flip_Flop d_ff_17 (.D(d_ff_5_q), .clk(and_23_out), .Q(d_ff_17_q));  // open: Qn, preset, reset
  and and_23 (and_23_out, and_21_out, d_ff_1_qn, clock_1_out);
  D_Flip_Flop d_ff_18 (.D(d_ff_6_q), .clk(and_24_out), .Q(d_ff_18_q));  // open: Qn, preset, reset
  and and_24 (and_24_out, and_21_out, d_ff_1_qn, clock_1_out);
  D_Flip_Flop d_ff_19 (.D(d_ff_7_q), .clk(and_25_out), .Q(d_ff_19_q));  // open: Qn, preset, reset
  and and_25 (and_25_out, and_21_out, d_ff_1_qn, clock_1_out);
  and and_26 (and_26_out, and_21_out, d_ff_1_q);
  and and_27 (and_27_out, d_ff_16_q, and_26_out);
  and and_28 (and_28_out, d_ff_17_q, and_26_out);
  and and_29 (and_29_out, d_ff_18_q, and_26_out);
  and and_30 (and_30_out, d_ff_19_q, and_26_out);
  not not_3 (not_3_out, d_ff_3_q);
  not not_4 (not_4_out, d_ff_2_q);
  and and_31 (and_31_out, not_3_out, not_4_out);
  D_Flip_Flop d_ff_20 (.D(d_ff_4_q), .clk(and_32_out), .Q(d_ff_20_q));  // open: Qn, preset, reset
  and and_32 (and_32_out, and_31_out, d_ff_1_qn, clock_1_out);
  D_Flip_Flop d_ff_21 (.D(d_ff_5_q), .clk(and_33_out), .Q(d_ff_21_q));  // open: Qn, preset, reset
  and and_33 (and_33_out, and_31_out, d_ff_1_qn, clock_1_out);
  D_Flip_Flop d_ff_22 (.D(d_ff_6_q), .clk(and_34_out), .Q(d_ff_22_q));  // open: Qn, preset, reset
  and and_34 (and_34_out, and_31_out, d_ff_1_qn, clock_1_out);
  D_Flip_Flop d_ff_23 (.D(d_ff_7_q), .clk(and_35_out), .Q(d_ff_23_q));  // open: Qn, preset, reset
  and and_35 (and_35_out, and_31_out, d_ff_1_qn, clock_1_out);
  and and_36 (and_36_out, and_31_out, d_ff_1_q);
  and and_37 (and_37_out, d_ff_20_q, and_36_out);
  and and_38 (and_38_out, d_ff_21_q, and_36_out);
  and and_39 (and_39_out, d_ff_22_q, and_36_out);
  and and_40 (and_40_out, d_ff_23_q, and_36_out);
  or or_1 (or_1_out, and_37_out, and_27_out, and_17_out, and_7_out);
  or or_2 (or_2_out, and_38_out, and_28_out, and_18_out, and_8_out);
  or or_3 (or_3_out, and_39_out, and_29_out, and_19_out, and_9_out);
  or or_4 (or_4_out, and_40_out, and_30_out, and_20_out, and_10_out);
  and and_41 (and_41_out, d_ff_1_q, clock_1_out);
  D_Flip_Flop d_ff_24 (.D(or_1_out), .clk(and_41_out), .Q(Output0));  // open: Qn, preset, reset
  D_Flip_Flop d_ff_25 (.D(or_2_out), .clk(and_41_out), .Q(Output1));  // open: Qn, preset, reset
  D_Flip_Flop d_ff_26 (.D(or_3_out), .clk(and_41_out), .Q(Output2));  // open: Qn, preset, reset
  D_Flip_Flop d_ff_27 (.D(or_4_out), .clk(and_41_out), .Q(Output3));  // open: Qn, preset, reset

  // Notes on the sheet:
  //   Address3
  //   Address3
  //   Address3
  //   Address3
  //   Address2
  //   Address2
  //   Address2
  //   Address2
  //   Address1
  //   Address1
  //   Address1
  //   Address1
  //   Address0
  //   Address0
  //   Address0
  //   Address0
endmodule

module MyALU (
  input  Operation1,
  input  AInvert,
  input  BInvert,
  input  Operation0,
  input  A0,
  input  B0,
  input  A1,
  input  B1,
  input  A2,
  input  B2,
  input  A3,
  input  B3,
  output Result0,
  output Result1,
  output Result2,
  output Result3,
  output Status0_Sign,
  output Status1_Zero,
  output Status2_SignOverflow
);

  wire and_1_out, and_2_out, and_3_out, and_4_out, and_5_out, and_6_out, and_7_out, and_8_out, and_9_out,
       and_10_out, and_11_out, and_12_out, and_13_out, and_14_out, and_15_out, and_16_out, and_17_out,
       and_18_out, and_19_out, and_20_out, and_21_out, and_22_out, and_23_out, and_24_out, and_25_out,
       and_26_out, and_27_out, and_28_out, and_29_out, and_30_out, and_31_out, and_32_out, and_33_out,
       and_34_out, and_35_out, and_36_out, and_37_out, and_38_out, and_39_out, and_40_out, and_41_out,
       and_42_out, and_43_out, and_44_out, and_45_out, and_46_out, and_47_out, and_48_out, and_49_out,
       and_50_out, and_51_out, and_52_out, and_53_out, and_54_out, and_55_out, clock_1_out, d_ff_1_q,
       d_ff_2_q, d_ff_3_q, d_ff_4_q, d_ff_5_q, d_ff_6_q, d_ff_7_q, d_ff_8_q, not_1_out, not_2_out, not_3_out,
       not_4_out, not_5_out, not_6_out, not_7_out, not_8_out, not_9_out, not_10_out, not_11_out, not_12_out,
       not_13_out, not_14_out, not_15_out, not_16_out, not_17_out, not_18_out, not_19_out, not_20_out,
       not_21_out, not_22_out, or_1_out, or_2_out, or_3_out, or_4_out, or_5_out, or_6_out, or_7_out,
       or_8_out, or_9_out, or_10_out, or_11_out, or_13_out, or_14_out, or_15_out, or_16_out, or_17_out,
       or_18_out, or_19_out, or_20_out, or_21_out, or_22_out, or_23_out, or_24_out, or_25_out, xor_1_out,
       xor_2_out, xor_3_out, xor_4_out, xor_5_out, xor_6_out, xor_7_out, xor_8_out, xor_9_out, xor_10_out;

  Clock #(.phaseOffset(1)) clock_1 (.out(clock_1_out));
  D_Flip_Flop d_ff_1 (.D(A0), .clk(clock_1_out), .Q(d_ff_1_q));  // open: Qn, preset, reset
  D_Flip_Flop d_ff_2 (.D(B0), .clk(clock_1_out), .Q(d_ff_2_q));  // open: Qn, preset, reset
  D_Flip_Flop d_ff_3 (.D(A1), .clk(clock_1_out), .Q(d_ff_3_q));  // open: Qn, preset, reset
  D_Flip_Flop d_ff_4 (.D(B1), .clk(clock_1_out), .Q(d_ff_4_q));  // open: Qn, preset, reset
  D_Flip_Flop d_ff_5 (.D(A2), .clk(clock_1_out), .Q(d_ff_5_q));  // open: Qn, preset, reset
  D_Flip_Flop d_ff_6 (.D(B2), .clk(clock_1_out), .Q(d_ff_6_q));  // open: Qn, preset, reset
  D_Flip_Flop d_ff_7 (.D(A3), .clk(clock_1_out), .Q(d_ff_7_q));  // open: Qn, preset, reset
  D_Flip_Flop d_ff_8 (.D(B3), .clk(clock_1_out), .Q(d_ff_8_q));  // open: Qn, preset, reset
  not not_1 (not_1_out, d_ff_1_q);
  not not_2 (not_2_out, d_ff_2_q);
  not not_3 (not_3_out, d_ff_3_q);
  not not_4 (not_4_out, d_ff_4_q);
  not not_5 (not_5_out, d_ff_5_q);
  not not_6 (not_6_out, d_ff_6_q);
  not not_7 (not_7_out, d_ff_7_q);
  not not_8 (not_8_out, d_ff_8_q);
  and and_1 (and_1_out, d_ff_1_q, not_9_out);
  not not_9 (not_9_out, AInvert);
  and and_2 (and_2_out, AInvert, not_1_out);
  and and_3 (and_3_out, d_ff_2_q, not_10_out);
  not not_10 (not_10_out, BInvert);
  and and_4 (and_4_out, BInvert, not_2_out);
  and and_5 (and_5_out, d_ff_3_q, not_11_out);
  not not_11 (not_11_out, AInvert);
  and and_6 (and_6_out, AInvert, not_3_out);
  and and_7 (and_7_out, d_ff_4_q, not_12_out);
  not not_12 (not_12_out, BInvert);
  and and_8 (and_8_out, BInvert, not_4_out);
  and and_9 (and_9_out, d_ff_5_q, not_13_out);
  not not_13 (not_13_out, AInvert);
  and and_10 (and_10_out, AInvert, not_5_out);
  and and_11 (and_11_out, d_ff_6_q, not_14_out);
  not not_14 (not_14_out, BInvert);
  and and_12 (and_12_out, BInvert, not_6_out);
  and and_13 (and_13_out, d_ff_7_q, not_15_out);
  not not_15 (not_15_out, AInvert);
  and and_14 (and_14_out, AInvert, not_7_out);
  and and_15 (and_15_out, d_ff_8_q, not_16_out);
  not not_16 (not_16_out, BInvert);
  and and_16 (and_16_out, BInvert, not_8_out);
  or or_1 (or_1_out, and_1_out, and_2_out);
  or or_2 (or_2_out, and_3_out, and_4_out);
  or or_3 (or_3_out, and_5_out, and_6_out);
  or or_4 (or_4_out, and_7_out, and_8_out);
  or or_5 (or_5_out, and_9_out, and_10_out);
  or or_6 (or_6_out, and_11_out, and_12_out);
  or or_7 (or_7_out, and_13_out, and_14_out);
  or or_8 (or_8_out, and_15_out, and_16_out);
  xor xor_1 (xor_1_out, or_1_out, or_2_out);
  and and_17 (and_17_out, or_2_out, or_1_out);
  xor xor_2 (xor_2_out, or_3_out, or_4_out);
  and and_18 (and_18_out, or_4_out, or_3_out);
  xor xor_3 (xor_3_out, or_5_out, or_6_out);
  and and_19 (and_19_out, or_6_out, or_5_out);
  xor xor_4 (xor_4_out, or_7_out, or_8_out);
  and and_20 (and_20_out, or_8_out, or_7_out);
  xor xor_5 (xor_5_out, BInvert, xor_1_out);
  and and_21 (and_21_out, xor_1_out, BInvert);
  xor xor_6 (xor_6_out, or_9_out, xor_2_out);
  and and_22 (and_22_out, xor_2_out, or_9_out);
  xor xor_7 (xor_7_out, or_10_out, xor_3_out);
  and and_23 (and_23_out, xor_3_out, or_10_out);
  xor xor_8 (xor_8_out, or_11_out, xor_4_out);
  and and_24 (and_24_out, xor_4_out, or_11_out);
  or or_9 (or_9_out, and_21_out, and_17_out);
  or or_10 (or_10_out, and_22_out, and_18_out);
  or or_11 (or_11_out, and_23_out, and_19_out);
  // OR_Gate or_12 has open pins: in0=and_24_out, in1=and_20_out, out=open
  not not_17 (not_17_out, Operation1);
  or or_13 (or_13_out, or_1_out, or_2_out);
  and and_25 (and_25_out, or_1_out, or_2_out);
  or or_14 (or_14_out, or_3_out, or_4_out);
  and and_26 (and_26_out, or_3_out, or_4_out);
  or or_15 (or_15_out, or_5_out, or_6_out);
  and and_27 (and_27_out, or_5_out, or_6_out);
  or or_16 (or_16_out, or_7_out, or_8_out);
  and and_28 (and_28_out, or_7_out, or_8_out);
  not not_18 (not_18_out, Operation0);
  and and_29 (and_29_out, xor_5_out, Operation1);
  and and_30 (and_30_out, or_13_out, not_17_out);
  and and_31 (and_31_out, and_25_out, not_17_out);
  and and_32 (and_32_out, xor_6_out, Operation1);
  and and_33 (and_33_out, or_14_out, not_17_out);
  and and_34 (and_34_out, and_26_out, not_17_out);
  and and_35 (and_35_out, xor_7_out, Operation1);
  and and_36 (and_36_out, or_15_out, not_17_out);
  and and_37 (and_37_out, and_27_out, not_17_out);
  and and_38 (and_38_out, xor_8_out, Operation1);
  and and_39 (and_39_out, or_16_out, not_17_out);
  and and_40 (and_40_out, and_28_out, not_17_out);
  and and_41 (and_41_out, and_29_out, not_18_out);
  and and_42 (and_42_out, Operation0, and_30_out);
  and and_43 (and_43_out, not_18_out, and_31_out);
  and and_44 (and_44_out, and_32_out, not_18_out);
  and and_45 (and_45_out, Operation0, and_33_out);
  and and_46 (and_46_out, not_18_out, and_34_out);
  and and_47 (and_47_out, and_35_out, not_18_out);
  and and_48 (and_48_out, Operation0, and_36_out);
  and and_49 (and_49_out, not_18_out, and_37_out);
  and and_50 (and_50_out, and_38_out, not_18_out);
  and and_51 (and_51_out, Operation0, and_39_out);
  and and_52 (and_52_out, not_18_out, and_40_out);
  or or_17 (or_17_out, and_41_out, and_42_out);
  or or_18 (or_18_out, and_44_out, and_45_out);
  or or_19 (or_19_out, and_47_out, and_48_out);
  or or_20 (or_20_out, and_50_out, and_51_out);
  or or_21 (or_21_out, or_17_out, and_43_out);
  or or_22 (or_22_out, or_18_out, and_46_out);
  or or_23 (or_23_out, or_19_out, and_49_out);
  or or_24 (or_24_out, or_20_out, and_52_out);
  D_Flip_Flop d_ff_9 (.D(or_21_out), .clk(clock_1_out), .Q(Result0));  // open: Qn, preset, reset
  D_Flip_Flop d_ff_10 (.D(or_22_out), .clk(clock_1_out), .Q(Result1));  // open: Qn, preset, reset
  D_Flip_Flop d_ff_11 (.D(or_23_out), .clk(clock_1_out), .Q(Result2));  // open: Qn, preset, reset
  D_Flip_Flop d_ff_12 (.D(or_24_out), .clk(clock_1_out), .Q(Result3));  // open: Qn, preset, reset
  xor xor_9 (xor_9_out, or_7_out, or_8_out);
  and and_53 (and_53_out, or_7_out, or_8_out);
  and and_54 (and_54_out, or_24_out, xor_9_out);
  not not_19 (not_19_out, or_21_out);
  not not_20 (not_20_out, or_22_out);
  not not_21 (not_21_out, or_23_out);
  not not_22 (not_22_out, or_24_out);
  or or_25 (or_25_out, and_54_out, and_53_out);
  and and_55 (and_55_out, not_19_out, not_20_out, not_21_out, not_22_out);
  xor xor_10 (xor_10_out, or_24_out, or_25_out);
  D_Flip_Flop d_ff_13 (.D(or_25_out), .clk(clock_1_out), .Q(Status0_Sign));  // open: Qn, preset, reset
  D_Flip_Flop d_ff_14 (.D(and_55_out), .clk(clock_1_out), .Q(Status1_Zero));  // open: Qn, preset, reset
  D_Flip_Flop d_ff_15 (.D(xor_10_out), .clk(clock_1_out), .Q(Status2_SignOverflow));  // open: Qn, preset, reset

  // Notes on the sheet:
  //   A0: initial=0x1
  //   B0: initial=0x1
  //   Multiplexor for inverting
  //    Full bit adder circuit
  //   Multiplexer to choose operation
endmodule
